# Fritzing sketch V5_Versuchsaufbau (saved by Fritzing 0.9.3b)
breadboards: 1

parts:
  Mod1 = Raspberry Pi Pico
  Mod2 = AD8232 HeartRate Monitor [part_number=SEN-12650]

nets:
  N1: Mod1.pin_3, Mod1.pin_8, Mod1.pin_13, Mod1.pin_18, Mod1.pin_23, Mod1.pin_28, Mod1.pin_33, Mod1.pin_38, Mod1.pin_42, Mod2.GND
  N2: Mod1.pin_31, Mod2.OUTPUT
  N3: Mod1.pin_36, Mod2.3.3v
  N4: Mod2.LA, Mod2.RL

custom parts:
  Raspberry Pi Pico: Raspberry Pi Pico. Based around the RP2040 microcontroller the Pico is a low cost microcontroller device bringing Raspberry Pi quality, cost, and easy of use to the microcontroller space. Jan 2021, Split part in to two versions: tht (this one) and SMD. This one will drill holes for a .1 in header in pcb to allow plugging in the module as well as providing pads to solder the module to the top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
  AD8232 HeartRate Monitor: Sparkfun single lead heart rate monitor - Ad8232.
